# Fritzing sketch seven-segment (saved by Fritzing 0.4.3b)
breadboards: 1

parts:
  Arduino1 = Arduino
  DI1 = 7-Segment LED Display [package=THT]
  R1 = Resistor [resistance=220 package=THT]
  R2 = Resistor [resistance=220 package=THT]

nets:
  N1: Arduino1.GND, R1.Pin_1, R2.Pin_1
  N2: Arduino1.D9, DI1.cathodeDP
  N3: Arduino1.D8, DI1.cathodeG
  N4: Arduino1.D7, DI1.cathodeF
  N5: Arduino1.D6, DI1.cathodeE
  N6: Arduino1.D5, DI1.cathodeD
  N7: Arduino1.D4, DI1.cathodeC
  N8: Arduino1.D3, DI1.cathodeB
  N9: Arduino1.D2, DI1.cathodeA
  N10: DI1.commAnode#2, R2.Pin_0
  N11: DI1.commAnode#7, R1.Pin_0

notes:
  Connecting a 7 segment Display (common anode) with an Arduino board.
  The following is the mapping from Arduino pin to 7 segment display
  2 => 7
  3 => 6
  4 => 4
  5 => 2
  6 => 1
  7 => 9
  8 => 10
  9 => 5
  https://github.com/sudar/arduino-sketches
